# Fritzing sketch Fritzing_NodeMCU_Ultrason (saved by Fritzing 0.9.3b)
breadboards: 1

parts:
  U1 = NodeMCU V1.0
  Componente1 = SRF05 Ultrasonic Rangefinder
  LED1 = LED - 5mm [color="Red (633nm)" package="5 mm [THT]"]
  R1 = Resistor [tolerance=±5% resistance=220 package=THT]
  LED2 = LED - 5mm [color="Red (633nm)" package="5 mm [THT]"]
  R2 = Resistor [tolerance=±5% resistance=220 package=THT]

nets:
  N1: U1.D1, R1.Pin_1
  N2: U1.D2, R2.Pin_1
  GND: U1.GND, Componente1.GND, LED1.cathode, LED2.cathode
  N3: U1.D5, Componente1.Trig
  N4: U1.D6, Componente1.Echo
  VIN: U1.Vin, Componente1.VCC
  N5: LED1.anode, R1.Pin_0
  N6: LED2.anode, R2.Pin_0

custom parts:
  NodeMCU V1.0: ESP8266 based NodeMCU
